// Logisim project Circuit.circ as structural Verilog: 2 circuits, main circuit main
module main (
);

  wire edge_triggered_d_type_flip_flop_1_q, edge_triggered_d_type_flip_flop_2_q,
       edge_triggered_d_type_flip_flop_3_q, edge_triggered_d_type_flip_flop_4_q,
       edge_triggered_d_type_flip_flop_5_q, edge_triggered_d_type_flip_flop_6_q,
       edge_triggered_d_type_flip_flop_7_q, edge_triggered_d_type_flip_flop_8_q,
       edge_triggered_d_type_flip_flop_9_q, edge_triggered_d_type_flip_flop_10_q,
       edge_triggered_d_type_flip_flop_11_q, edge_triggered_d_type_flip_flop_12_q,
       edge_triggered_d_type_flip_flop_13_q, edge_triggered_d_type_flip_flop_14_q,
       edge_triggered_d_type_flip_flop_15_q, edge_triggered_d_type_flip_flop_16_q, x1_1_out, x2_2_out,
       x4_4_out, x8_8_out, x16_16_out, x32_32_out, x64_64_out, x128_128_out, x256_256_out, x512_512_out,
       x1024_1024_out, x2048_2048_out, x4096_4096_out, x16384_16384_out, x32768_32768_out, x65536_65536_out,
       x131072_131072_out;

  Clock #(.highDuration(131072), .lowDuration(131072)) x131072_131072 (.out(x131072_131072_out));
  Clock #(.highDuration(65536), .lowDuration(65536)) x65536_65536 (.out(x65536_65536_out));
  Clock #(.highDuration(32768), .lowDuration(32768)) x32768_32768 (.out(x32768_32768_out));
  Clock #(.highDuration(16384), .lowDuration(16384)) x16384_16384 (.out(x16384_16384_out));
  Clock #(.highDuration(4096), .lowDuration(4096)) x4096_4096 (.out(x4096_4096_out));
  Clock #(.highDuration(2048), .lowDuration(2048)) x2048_2048 (.out(x2048_2048_out));
  Clock #(.highDuration(1024), .lowDuration(1024)) x1024_1024 (.out(x1024_1024_out));
  Clock #(.highDuration(512), .lowDuration(512)) x512_512 (.out(x512_512_out));
  Clock #(.highDuration(256), .lowDuration(256)) x256_256 (.out(x256_256_out));
  Clock #(.highDuration(128), .lowDuration(128)) x128_128 (.out(x128_128_out));
  Clock #(.highDuration(64), .lowDuration(64)) x64_64 (.out(x64_64_out));
  Clock #(.highDuration(32), .lowDuration(32)) x32_32 (.out(x32_32_out));
  Clock #(.highDuration(16), .lowDuration(16)) x16_16 (.out(x16_16_out));
  Clock #(.highDuration(8), .lowDuration(8)) x8_8 (.out(x8_8_out));
  Clock #(.highDuration(4), .lowDuration(4)) x4_4 (.out(x4_4_out));
  Clock #(.highDuration(2), .lowDuration(2)) x2_2 (.out(x2_2_out));
  Clock x1_1 (.out(x1_1_out));
  edge_triggered_D_type_flip_flop edge_triggered_d_type_flip_flop_1 (
    .D(x65536_65536_out), .Clk(x1_1_out), .Q(edge_triggered_d_type_flip_flop_1_q));  // open: Q_prime
  edge_triggered_D_type_flip_flop edge_triggered_d_type_flip_flop_2 (
    .D(x16384_16384_out), .Clk(x1_1_out), .Q(edge_triggered_d_type_flip_flop_2_q));  // open: Q_prime
  edge_triggered_D_type_flip_flop edge_triggered_d_type_flip_flop_3 (
    .D(x2048_2048_out), .Clk(x1_1_out), .Q(edge_triggered_d_type_flip_flop_3_q));  // open: Q_prime
  edge_triggered_D_type_flip_flop edge_triggered_d_type_flip_flop_4 (
    .D(x512_512_out), .Clk(x1_1_out), .Q(edge_triggered_d_type_flip_flop_4_q));  // open: Q_prime
  edge_triggered_D_type_flip_flop edge_triggered_d_type_flip_flop_5 (
    .D(x128_128_out), .Clk(x1_1_out), .Q(edge_triggered_d_type_flip_flop_5_q));  // open: Q_prime
  edge_triggered_D_type_flip_flop edge_triggered_d_type_flip_flop_6 (
    .D(x32_32_out), .Clk(x1_1_out), .Q(edge_triggered_d_type_flip_flop_6_q));  // open: Q_prime
  edge_triggered_D_type_flip_flop edge_triggered_d_type_flip_flop_7 (
    .D(x8_8_out), .Clk(x1_1_out), .Q(edge_triggered_d_type_flip_flop_7_q));  // open: Q_prime
  edge_triggered_D_type_flip_flop edge_triggered_d_type_flip_flop_8 (
    .D(x2_2_out), .Clk(x1_1_out), .Q(edge_triggered_d_type_flip_flop_8_q));  // open: Q_prime
  edge_triggered_D_type_flip_flop edge_triggered_d_type_flip_flop_9 (
    .D(x131072_131072_out), .Clk(x1_1_out), .Q(edge_triggered_d_type_flip_flop_9_q));  // open: Q_prime
  edge_triggered_D_type_flip_flop edge_triggered_d_type_flip_flop_10 (
    .D(x32768_32768_out), .Clk(x1_1_out), .Q(edge_triggered_d_type_flip_flop_10_q));  // open: Q_prime
  edge_triggered_D_type_flip_flop edge_triggered_d_type_flip_flop_11 (
    .D(x4096_4096_out), .Clk(x1_1_out), .Q(edge_triggered_d_type_flip_flop_11_q));  // open: Q_prime
  edge_triggered_D_type_flip_flop edge_triggered_d_type_flip_flop_12 (
    .D(x1024_1024_out), .Clk(x1_1_out), .Q(edge_triggered_d_type_flip_flop_12_q));  // open: Q_prime
  edge_triggered_D_type_flip_flop edge_triggered_d_type_flip_flop_13 (
    .D(x256_256_out), .Clk(x1_1_out), .Q(edge_triggered_d_type_flip_flop_13_q));  // open: Q_prime
  edge_triggered_D_type_flip_flop edge_triggered_d_type_flip_flop_14 (
    .D(x64_64_out), .Clk(x1_1_out), .Q(edge_triggered_d_type_flip_flop_14_q));  // open: Q_prime
  edge_triggered_D_type_flip_flop edge_triggered_d_type_flip_flop_15 (
    .D(x16_16_out), .Clk(x1_1_out), .Q(edge_triggered_d_type_flip_flop_15_q));  // open: Q_prime
  edge_triggered_D_type_flip_flop edge_triggered_d_type_flip_flop_16 (
    .D(x4_4_out), .Clk(x1_1_out), .Q(edge_triggered_d_type_flip_flop_16_q));  // open: Q_prime
  LED Q15 (.in(edge_triggered_d_type_flip_flop_9_q));
  LED Q14 (.in(edge_triggered_d_type_flip_flop_1_q));
  LED Q13 (.in(edge_triggered_d_type_flip_flop_10_q));
  LED Q12 (.in(edge_triggered_d_type_flip_flop_2_q));
  LED Q11 (.in(edge_triggered_d_type_flip_flop_11_q));
  LED Q10 (.in(edge_triggered_d_type_flip_flop_3_q));
  LED Q9 (.in(edge_triggered_d_type_flip_flop_12_q));
  LED Q8 (.in(edge_triggered_d_type_flip_flop_4_q));
  LED Q7 (.in(edge_triggered_d_type_flip_flop_13_q));
  LED Q6 (.in(edge_triggered_d_type_flip_flop_5_q));
  LED Q5 (.in(edge_triggered_d_type_flip_flop_14_q));
  LED Q4 (.in(edge_triggered_d_type_flip_flop_6_q));
  LED Q3 (.in(edge_triggered_d_type_flip_flop_15_q));
  LED Q2 (.in(edge_triggered_d_type_flip_flop_7_q));
  LED Q1 (.in(edge_triggered_d_type_flip_flop_16_q));
  LED Q0 (.in(edge_triggered_d_type_flip_flop_8_q));
endmodule

module edge_triggered_D_type_flip_flop (
  input  D,
  input  Clk,
  output Q,
  output Q_prime
);

  wire and_1_out, and_2_out, and_3_out, and_4_out, nor_1_out, nor_2_out, not_1_out, not_2_out;

  not not_1 (not_1_out, Clk);
  and and_1 (and_1_out, D, not_1_out);
  and and_2 (and_2_out, not_1_out, not_2_out);
  not not_2 (not_2_out, D);
  nor nor_1 (nor_1_out, and_1_out, nor_2_out);
  nor nor_2 (nor_2_out, nor_1_out, and_2_out);
  and and_3 (and_3_out, nor_1_out, Clk);
  and and_4 (and_4_out, Clk, nor_2_out);
  nor nor_3 (Q, and_3_out, Q_prime);
  nor nor_4 (Q_prime, Q, and_4_out);
endmodule
